// Logisim project logisim_cpu.circ as structural Verilog: 4 circuits, main circuit main
module main (
  input  in_1,
  input  [7:0] in_2,
  output [7:0] out_3
);

  wire and_1_out, clock_1_out, compute, Cond, cond_1_cout, controlled_buffer_1_out, CP, decoder_1_out0,
       decoder_1_out1, decoder_1_out2, decoder_1_out3, decoder_1_out4, decoder_1_out5, decoder_1_out6,
       decoder_2_out0, decoder_2_out1, decoder_2_out2, decoder_2_out3, decoder_2_out4, decoder_2_out5,
       decoder_2_out6, IM, or_1_out, or_2_out;
  wire [7:0] allBits, alu_1_aluout, controlled_buffer_2_out, counter_1_q, DBUS, REG0_aout, REG2_aout,
       REG3_aout, REG4;

  Clock clock_1 (.out(clock_1_out));
  assign controlled_buffer_1_out = Cond ? cond_1_cout : 1'bz;  // Controlled_Buffer controlled_buffer_1
  COND cond_1 (.Vinp(REG4), .Cin(DBUS), .Cout(cond_1_cout));
  Counter counter_1 (
    .load(Cond), .clk(and_1_out), .D(controlled_buffer_2_out), .Q(counter_1_q));  // open: clr, up, count, carry
  and and_1 (and_1_out, clock_1_out, in_1);
  assign controlled_buffer_2_out = controlled_buffer_1_out ? REG0_aout : 8'bz;  // Controlled_Buffer controlled_buffer_2
  Decoder #(.select(3)) decoder_1 (
    .out0(decoder_1_out0), .out1(decoder_1_out1), .out2(decoder_1_out2), .out3(decoder_1_out3),
    .out4(decoder_1_out4), .out5(decoder_1_out5), .out6(decoder_1_out6), .sel(allBits[2:0]), .en(CP));  // open: out7
  or or_1 (or_1_out, decoder_1_out0, IM);
  or or_2 (or_2_out, compute, decoder_1_out3);
  assign DBUS = decoder_1_out6 ? in_2 : 8'bz;  // Controlled_Buffer controlled_buffer_3
  Decoder #(.select(3)) decoder_2 (
    .out0(decoder_2_out0), .out1(decoder_2_out1), .out2(decoder_2_out2), .out3(decoder_2_out3),
    .out4(decoder_2_out4), .out5(decoder_2_out5), .out6(decoder_2_out6), .sel(allBits[5:3]), .en(CP));  // open: out7
  ROM rom_1 (.addr(counter_1_q), .data(allBits));
  register_but_better REG0 (.Rinp(DBUS), .Load(or_1_out), .EnableOut(decoder_2_out0), .Rout(DBUS), .AOUT(REG0_aout));
  register_but_better REG2 (
    .Rinp(DBUS), .Load(decoder_1_out1), .EnableOut(decoder_2_out1), .Rout(DBUS), .AOUT(REG2_aout));
  register_but_better REG3 (
    .Rinp(DBUS), .Load(decoder_1_out2), .EnableOut(decoder_2_out2), .Rout(DBUS), .AOUT(REG3_aout));
  register_but_better RE4G (.Rinp(DBUS), .Load(or_2_out), .EnableOut(decoder_2_out3), .Rout(DBUS), .AOUT(REG4));
  register_but_better REG5 (.Rinp(DBUS), .Load(decoder_1_out4), .EnableOut(decoder_2_out4), .Rout(DBUS));  // open: AOUT
  register_but_better REG6 (.Rinp(DBUS), .Load(decoder_1_out5), .EnableOut(decoder_2_out5), .Rout(DBUS));  // open: AOUT
  assign DBUS = compute ? alu_1_aluout : 8'bz;  // Controlled_Buffer controlled_buffer_4
  assign out_3 = decoder_2_out6 ? DBUS : 8'bz;  // Controlled_Buffer controlled_buffer_5
  ALU alu_1 (.opcode(allBits), .A(REG2_aout), .B(REG3_aout), .ALUout(alu_1_aluout));
  Decoder #(.select(2)) decoder_3 (.out0(IM), .out1(CP), .out2(compute), .out3(Cond), .sel(allBits[7:6]));  // open: en

  // Other names for the same wires on the sheet: cpins[2:0] = allBits[5:3]; ldins[2:0] = allBits[2:0]

  // Notes on the sheet:
  //   load
  //   CP
  //   contents of rom_1 (hex, n*v repeats v):
  //   0 c4
endmodule

module ALU (
  input  [7:0] opcode,
  input  [7:0] A,
  input  [7:0] B,
  output [7:0] ALUout
);

  wire comparator_1_eq, comparator_2_eq, comparator_3_eq, comparator_4_eq, comparator_5_eq, comparator_6_eq,
       comparator_7_eq;
  wire [7:0] adder_1_out, and_1_out, controlled_buffer_1_out, multiplier_1_out, or_1_out, subtractor_1_out,
       xor_1_out;

  assign controlled_buffer_1_out = comparator_1_eq ? adder_1_out : 8'bz;  // Controlled_Buffer controlled_buffer_1
  Adder adder_1 (.a(B), .b(A), .out(adder_1_out));  // open: cin, cout
  assign controlled_buffer_1_out = comparator_3_eq ? subtractor_1_out : 8'bz;  // Controlled_Buffer controlled_buffer_2
  Subtractor subtractor_1 (.a(B), .b(A), .out(subtractor_1_out));  // open: bin, bout
  assign and_1_out = B & A;  // AND_Gate and_1, 8 bits wide
  Multiplier #(.mode("twosComplement")) multiplier_1 (.a(B), .b(A), .out(multiplier_1_out));  // open: cin, cout
  assign or_1_out = B | A;  // OR_Gate or_1, 8 bits wide
  assign xor_1_out = B ^ A;  // XOR_Gate xor_1, 8 bits wide
  Comparator comparator_1 (.a(8'h2), .b(opcode), .eq(comparator_1_eq));  // open: gt, lt
  Comparator comparator_2 (.a(8'h3), .b(opcode), .eq(comparator_2_eq));  // open: gt, lt
  assign controlled_buffer_1_out = comparator_2_eq ? and_1_out : 8'bz;  // Controlled_Buffer controlled_buffer_3
  Comparator comparator_3 (.a(8'h4), .b(opcode), .eq(comparator_3_eq));  // open: gt, lt
  assign controlled_buffer_1_out = comparator_4_eq ? multiplier_1_out : 8'bz;  // Controlled_Buffer controlled_buffer_4
  Comparator comparator_4 (.a(8'h5), .b(opcode), .eq(comparator_4_eq), .lt(comparator_4_eq));  // open: gt
  assign controlled_buffer_1_out = comparator_5_eq ? or_1_out : 8'bz;  // Controlled_Buffer controlled_buffer_5
  Comparator comparator_5 (.a(8'h6), .b(opcode), .eq(comparator_5_eq));  // open: gt, lt
  assign controlled_buffer_1_out = comparator_6_eq ? or_1_out : 8'bz;  // Controlled_Buffer controlled_buffer_6
  Comparator comparator_6 (.a(8'h7), .b(opcode), .eq(comparator_6_eq));  // open: gt, lt
  assign ALUout = comparator_6_eq ? ~controlled_buffer_1_out : 8'bz;  // Controlled_Inverter controlled_inverter_1
  assign ALUout = comparator_7_eq ? xor_1_out : 8'bz;  // Controlled_Buffer controlled_buffer_7
  Comparator comparator_7 (.a(8'h8), .b(opcode), .eq(comparator_7_eq), .lt(comparator_7_eq));  // open: gt
endmodule

module register_but_better (
  input  EnableOut,
  input  [7:0] Rinp,
  input  Load,
  output [7:0] Rout,
  output [7:0] AOUT
);

  Register register_1 (.D(Rinp), .en(1'b1), .clk(Load), .Q(AOUT));  // open: clr
  assign Rout = EnableOut ? AOUT : 8'bz;  // Controlled_Buffer controlled_buffer_1
endmodule

module COND (
  input  [7:0] Cin,
  input  [7:0] Vinp,
  output Cout
);

  wire comparator_1_eq, comparator_1_gt, comparator_1_lt, controlled_buffer_1_out, controlled_inverter_1_out,
       decoder_1_out1, decoder_1_out2, decoder_1_out4, decoder_1_out5, decoder_1_out6, decoder_1_out7, never,
       not_1_out, or_1_out, or_2_out, or_3_out;

  assign controlled_buffer_1_out = decoder_1_out6 ? or_1_out : 1'bz;  // Controlled_Buffer controlled_buffer_1
  or or_1 (or_1_out, comparator_1_gt, comparator_1_eq);
  Comparator comparator_1 (.a(Vinp), .b({8{1'b0}}), .gt(comparator_1_gt), .eq(comparator_1_eq), .lt(comparator_1_lt));
  assign controlled_buffer_1_out = decoder_1_out7 ? comparator_1_gt : 1'bz;  // Controlled_Buffer controlled_buffer_2
  Decoder #(.select(3)) decoder_1 (
    .out0(never), .out1(decoder_1_out1), .out2(decoder_1_out2), .out3(controlled_buffer_1_out),
    .out4(decoder_1_out4), .out5(decoder_1_out5), .out6(decoder_1_out6), .out7(decoder_1_out7), .sel(Cin[2:0]));  // open: en
  assign controlled_buffer_1_out = decoder_1_out1 ? comparator_1_eq : 1'bz;  // Controlled_Buffer controlled_buffer_3
  or or_2 (or_2_out, comparator_1_eq, comparator_1_lt);
  assign controlled_buffer_1_out = decoder_1_out2 ? comparator_1_lt : 1'bz;  // Controlled_Buffer controlled_buffer_4
  assign controlled_buffer_1_out = controlled_buffer_1_out ? or_2_out : 1'bz;  // Controlled_Buffer controlled_buffer_5
  not not_1 (not_1_out, comparator_1_eq);
  assign controlled_buffer_1_out = decoder_1_out5 ? not_1_out : 1'bz;  // Controlled_Buffer controlled_buffer_6
  or or_3 (or_3_out, never, decoder_1_out4);
  assign controlled_inverter_1_out = or_3_out ? ~controlled_buffer_1_out : 1'bz;  // Controlled_Inverter controlled_inverter_1
  or or_4 (Cout, decoder_1_out4, controlled_inverter_1_out);
endmodule
